# Fritzing sketch Fritzing File (saved by Fritzing 0.9.3b)
breadboards: 1

parts:
  Max1 = chipKIT Max32 [chip_label=IC package="SIP (Single Inline) [THT]"]
  Raspberry_Pi_1 = Raspberry Pi 3 [part_number=RPI-3-V1.2]  # not connected
  U2 = XBEE-1 [package=xbee-silk]  # not connected
  USBTTL1 = Micro USB B Plug
  USBTTL2 = USB A Plug
  LED1 = RGB LED (com. cathode, rbg) [package="5 mm [THT]"]
  LED2 = RGB LED (com. cathode, rbg) [package="5 mm [THT]"]
  LED3 = RGB LED (com. cathode, rbg) [package="5 mm [THT]"]
  16-Channel_Servo_Controller1 = 16-Channel Servo Controller [part_number="16-Channel Servo Controller" package="DIP (Dual Inline) [THT]"]
  J4 = Basic Servo
  J5 = Basic Servo
  J6 = Basic Servo
  hc-sr1 = hc-sr04
  hc-sr2 = hc-sr04
  hc-sr3 = hc-sr04
  Part2 = SKXBEE R2  # not connected
  D2F1 = D2F-FL Omron Snap Action Limit Switch with Level
  R1 = Resistor [tolerance=±5% resistance=10k package=THT]
  R2 = Resistor [tolerance=±5% resistance=10k package=THT]
  R3 = Resistor [tolerance=±5% resistance=10k package=THT]
  D2F2 = D2F-FL Omron Snap Action Limit Switch with Level
  D2F3 = D2F-FL Omron Snap Action Limit Switch with Level
  M1 = cytron XBee shield
  U3 = XBEE-1 [package=xbee-silk]  # not connected

nets:
  VCC: Max1.5V, 16-Channel_Servo_Controller1.+3v3, hc-sr1.VCC, hc-sr2.VCC, hc-sr3.VCC, R1.Pin_1, R2.Pin_1, R3.Pin_1
  N1: Max1.A0, M1.A0
  N2: Max1.A1, M1.A1
  N3: Max1.A2, M1.A2
  N4: Max1.A3, M1.A3
  N5: Max1.A4, M1.A4
  N6: Max1.A5, M1.A5
  N7: Max1.D0, M1.RX0/D0
  N8: Max1.D1, M1.TX0/D1
  N9: Max1.D2, M1.D2
  N10: Max1.D3, LED3.green_anode, M1.~D3
  N11: Max1.D4, LED3.blue_anode, M1.D4
  N12: Max1.D5, LED3.red_anode, M1.~D5
  N13: Max1.D6, LED2.green_anode, M1.~D6
  N14: Max1.D7, LED2.blue_anode, M1.D7
  N15: Max1.D8, LED2.red_anode, M1.D8
  N16: Max1.D9, LED1.green_anode, M1.~D9
  N17: Max1.D10, M1.~D10
  N18: Max1.D11, M1.~D11
  N19: Max1.D12, LED1.blue_anode, M1.D12
  N20: Max1.D13, LED1.red_anode, M1.D13
  N21: Max1.D18, 16-Channel_Servo_Controller1.RX
  N22: Max1.D19, 16-Channel_Servo_Controller1.TX
  N23: Max1.D22, R1.Pin_0, D2F3.NO
  N24: Max1.D23, D2F1.NO, R2.Pin_0
  N25: Max1.D30, R3.Pin_0, D2F2.NO
  N26: Max1.D36, hc-sr3.Trig
  N27: Max1.D37, hc-sr3.Echo
  N28: Max1.D40, hc-sr2.Trig
  N29: Max1.D41, hc-sr2.Echo
  N30: Max1.D44, hc-sr1.Trig
  N31: Max1.D45, hc-sr1.Echo
  GND: Max1.GND, M1.GND
  N32: USBTTL1.usb, USBTTL2.usb
  GND_2: LED1.common_cathode, LED2.common_cathode, LED3.common_cathode, 16-Channel_Servo_Controller1.GND#3, hc-sr1.GND, hc-sr2.GND, hc-sr3.GND, D2F1.COM, D2F2.COM, D2F3.COM
  N33: 16-Channel_Servo_Controller1.S0, J6.pulse
  N34: 16-Channel_Servo_Controller1.VCC#7, J6.vcc
  N35: 16-Channel_Servo_Controller1.GND#8, J6.gnd
  N36: 16-Channel_Servo_Controller1.S1, J5.pulse
  N37: 16-Channel_Servo_Controller1.VCC#10, J5.vcc
  N38: 16-Channel_Servo_Controller1.GND#11, J5.gnd
  N39: 16-Channel_Servo_Controller1.S2, J4.pulse
  N40: 16-Channel_Servo_Controller1.VCC#13, J4.vcc
  N41: 16-Channel_Servo_Controller1.GND#14, J4.gnd
  N42: M1.D1-1, M1.D1-2
  N43: M1.D0-1, M1.D0-2

custom parts:
  chipKIT Max32: chipKIT's Max32
  16-Channel Servo Controller: Independent control of up to 16 RC servo motor in a single board. 1uS pulse width resolution. Serial TTL level UART I/O port interfaces easily with most microcontrollers, including gizDuino (Arduino Compatible Board). Easy to use command set. Additional Power Modules : Servo Soft Starter
  D2F-FL Omron Snap Action Limit Switch with Level: Snap action switch with stainless steel lever.
  cytron XBee shield: .This is the newly designed XBee Shield. It comes WITHOUT XBee module offering freedom to choose which ever compatible Xbee module you like to use :) It is a XBee expansion board that design for Arduino and you need to buy a XBee module separately.
